// Digital circuit ALU.dig as structural Verilog
module ALU (
  input  [31:0] A,
  input  [31:0] B,
  input  [3:0] ALUOp,
  output [31:0] R,
  output N,
  output Z,
  output C,
  output [3:0] NZCV,
  output V
);

  wire and_2_out, and_3_out, and_4_out, and_5_out, and_6_out, and_7_out, and_8_out, and_9_out, and_10_out,
       and_11_out;
  wire [31:0] add, \and , mul, rsb, sub;
  wire [63:32] mul_1_mul;

  Mul #(.Bits(32)) mul_1 (.a(A), .b(B), .mul({mul_1_mul, mul}));
  Add #(.Bits(32)) add_1 (.a(A), .b(B), .c_i(1'b0), .s(add));  // open: c_o
  Sub #(.Bits(32)) sub_1 (.a(A), .b(B), .c_i(1'b0), .s(sub));  // open: c_o
  Sub #(.Bits(32)) sub_2 (.a(B), .b(A), .c_i(1'b0), .s(rsb));  // open: c_o
  assign \and  = A & B;  // And and_1, 32 bits wide
  Multiplexer #(.Selector_Bits(4), .Bits(32)) multiplexer_1 (
    .sel(ALUOp), .in_0(add), .in_1(sub), .in_2(rsb), .in_3(mul), .in_4(B), .in_5(\and ), .in_6({32{1'b0}}),
    .in_7({32{1'b0}}), .in_8({32{1'b0}}), .in_9({32{1'b0}}), .in_10({32{1'b0}}), .in_11({32{1'b0}}),
    .in_12({32{1'b0}}), .in_13({32{1'b0}}), .in_14({32{1'b0}}), .in_15({32{1'b0}}), .out({N, R[30:0]}));
  and and_2 (and_2_out, ~A[31], 1'b1);  // And
  and and_3 (and_3_out, B[31], 1'b1);
  and and_4 (and_4_out, N, 1'b1);
  and and_5 (and_5_out, A[31], 1'b1);
  and and_6 (and_6_out, ~B[31], 1'b1);  // And
  and and_7 (and_7_out, ~N, 1'b1);  // And
  Comparator #(.Bits(32)) comparator_1 (.a({N, R[30:0]}), .b({32{1'b0}}), .eq(Z));  // open: gt, lt
  Comparator #(.Bits(32)) comparator_2 (.a(B), .b(A), .gt(C));  // open: eq, lt
  and and_8 (and_8_out, and_2_out, and_3_out);
  and and_9 (and_9_out, and_5_out, and_6_out);
  NZCV nzcv_1 (.N(N), .Z(Z), .C(C), .V(V), .NZCV(NZCV));
  and and_10 (and_10_out, and_8_out, and_4_out);
  and and_11 (and_11_out, and_9_out, and_7_out);
  or or_1 (V, and_10_out, and_11_out);

  assign R[31] = N;

  // Other names for the same wires on the sheet: sign_a = A[31]; mov[31:0] = B; sign_b = B[31]; sign_r = N

  // Notes on the sheet:
  //   Mov
  //   (0) 0000: add
  //   (1) 0001: sub
  //   (2) 0010: rsb
  //   (3) 0011:mul
  //   (4) 0100:mov
  //   (5) 0101: and
endmodule
