// Digital circuit B.dig as structural Verilog
module B (
  input  [31:0] IW,
  output [31:0] D,
  output [31:0] D_1
);

  BitExtender #(.inputBits(24), .outputBits(32)) bitextender_1 (.in(IW[23:0]), .out(D_1));

  assign D = {{9{IW[23]}}, IW[22:0]};
endmodule
