// Digital circuit NZCV.dig as structural Verilog
module NZCV (
  input  N,
  input  Z,
  input  C,
  input  V,
  output [3:0] NZCV
);

  wire [3:0] add_1_s, add_2_s;
  wire [7:0] mul_1_mul, mul_2_mul, mul_3_mul;

  Mul #(.Bits(4)) mul_1 (.a({3'b000, Z}), .b(4'b0010), .mul(mul_1_mul));
  Mul #(.Bits(4)) mul_2 (.a({3'b000, C}), .b(4'b0100), .mul(mul_2_mul));
  Mul #(.Bits(4)) mul_3 (.a({3'b000, V}), .b(4'b1000), .mul(mul_3_mul));
  Add #(.Bits(4)) add_1 (.a({3'b000, N}), .b(mul_1_mul[3:0]), .c_i(1'b0), .s(add_1_s));  // open: c_o
  Add #(.Bits(4)) add_2 (.a(add_1_s), .b(mul_2_mul[3:0]), .c_i(1'b0), .s(add_2_s));  // open: c_o
  Add #(.Bits(4)) add_3 (.a(add_2_s), .b(mul_3_mul[3:0]), .c_i(1'b0), .s(NZCV));  // open: c_o
endmodule
