// Digital circuit PC.dig as structural Verilog
module PC (
  input  [31:0] D,
  input  CLK,
  input  EN,
  input  CLR,
  output [31:0] Q
);

  digital_register_clr digital_register_clr_1 (.D(D), .CLK(CLK), .EN(EN), .CLR(CLR), .Q(Q));
endmodule
