// Digital circuit control-unit.dig as structural Verilog
module control_unit (
  input  [31:0] IW,
  input  [3:0] NZCV,
  input  CLK,
  output RFW,
  output [1:0] EXTop,
  output ALUsrcB,
  output [3:0] ALUop,
  output [1:0] PCsel,
  output [1:0] RR0sel,
  output RR1sel,
  output RR2sel,
  output WRsel,
  output WDsel,
  output sdt_i,
  output SHsel,
  output str,
  output ldr,
  output dp_i,
  output mul_i,
  output \byte 
);

  wire AL_eq, and_1_out, and_2_out, and_3_out, and_4_out, and_5_out, and_6_out, and_7_out, C,
       comparator_1_eq, comparator_2_lt, comparator_3_gt, comparator_4_eq, comparator_5_eq, comparator_6_eq,
       comparator_7_lt, comparator_8_gt, condex, decoder_part2_1_cpsrw, EQ_eq, GE_eq, GT_eq, LE_eq, LT_eq, N,
       NE_eq, or_1_out, or_2_out, or_3_out, V, Z;
  wire [1:0] PCsel_t;

  Comparator #(.Bits(4)) AL (.a(IW[31:28]), .b(4'b1110), .eq(AL_eq));  // open: gt, lt
  Comparator #(.Bits(4)) EQ (.a(IW[31:28]), .b(4'b0000), .eq(EQ_eq));  // open: gt, lt
  Comparator #(.Bits(4)) NE (.a(IW[31:28]), .b(4'b0001), .eq(NE_eq));  // open: gt, lt
  Comparator #(.Bits(4)) GE (.a(IW[31:28]), .b(4'b1010), .eq(GE_eq));  // open: gt, lt
  Comparator #(.Bits(4)) LT (.a(IW[31:28]), .b(4'b1011), .eq(LT_eq));  // open: gt, lt
  Comparator #(.Bits(4)) GT (.a(IW[31:28]), .b(4'b1100), .eq(GT_eq));  // open: gt, lt
  Comparator #(.Bits(4)) LE (.a(IW[31:28]), .b(4'b1101), .eq(LE_eq));  // open: gt, lt
  Register #(.Bits(4)) register_1 (.D(NZCV), .C(CLK), .en(decoder_part2_1_cpsrw), .Q({V, C, Z, N}));
  and and_1 (and_1_out, Z, EQ_eq);
  and and_2 (and_2_out, ~Z, NE_eq);  // And
  Comparator comparator_1 (.a(N), .b(V), .eq(comparator_1_eq));  // open: gt, lt
  Comparator comparator_2 (.a(N), .b(V), .lt(comparator_2_lt));  // open: gt, eq
  Comparator comparator_3 (.a(N), .b(V), .gt(comparator_3_gt));  // open: eq, lt
  Comparator comparator_4 (.a(Z), .b(1'b0), .eq(comparator_4_eq));  // open: gt, lt
  Comparator comparator_5 (.a(N), .b(V), .eq(comparator_5_eq));  // open: gt, lt
  Comparator comparator_6 (.a(Z), .b(1'b1), .eq(comparator_6_eq));  // open: gt, lt
  Comparator comparator_7 (.a(N), .b(V), .lt(comparator_7_lt));  // open: gt, eq
  Comparator comparator_8 (.a(N), .b(V), .gt(comparator_8_gt));  // open: eq, lt
  decoder_part2 decoder_part2_1 (
    .IW(IW), .RFW(RFW), .EXTop(EXTop), .ALUsrcB(ALUsrcB), .ALUop(ALUop), .PCsel(PCsel_t), .RR0sel(RR0sel),
    .RR1sel(RR1sel), .RR2sel(RR2sel), .WRsel(WRsel), .WDsel(WDsel), .SHsel(SHsel),
    .CPSRW(decoder_part2_1_cpsrw), .str(str), .ldr(ldr), .\byte (\byte ), .sdt_i(sdt_i), .dp_i(dp_i),
    .mul_i(mul_i));
  and and_3 (and_3_out, comparator_1_eq, GE_eq);
  or or_1 (or_1_out, comparator_2_lt, comparator_3_gt);
  and and_4 (and_4_out, comparator_4_eq, comparator_5_eq);
  or or_2 (or_2_out, comparator_7_lt, comparator_8_gt);
  and and_5 (and_5_out, or_1_out, LT_eq);
  and and_6 (and_6_out, and_4_out, GT_eq);
  or or_3 (or_3_out, comparator_6_eq, or_2_out);
  and and_7 (and_7_out, or_3_out, LE_eq);
  or or_4 (condex, AL_eq, and_1_out, and_2_out, and_3_out, and_5_out, and_6_out, and_7_out);
  Multiplexer #(.Bits(2)) multiplexer_1 (.sel(condex), .in_0(2'b00), .in_1(PCsel_t), .out(PCsel));

  // Other names for the same wires on the sheet: cond[3:0] = IW[31:28]
endmodule
