// Digital circuit decoder-en.dig as structural Verilog
module decoder_en (
  input  [3:0] SEL,
  input  EN,
  output EN0,
  output EN1,
  output EN2,
  output EN3,
  output EN4,
  output EN5,
  output EN6,
  output EN7,
  output EN8,
  output EN9,
  output EN10,
  output EN11,
  output EN12,
  output EN13,
  output EN14,
  output EN15
);

  wire decoder_1_out_0, decoder_1_out_1, decoder_1_out_2, decoder_1_out_3, decoder_1_out_4, decoder_1_out_5,
       decoder_1_out_6, decoder_1_out_7, decoder_1_out_8, decoder_1_out_9, decoder_1_out_10,
       decoder_1_out_11, decoder_1_out_12, decoder_1_out_13, decoder_1_out_14, decoder_1_out_15;

  Decoder #(.Selector_Bits(4)) decoder_1 (
    .sel(SEL), .out_0(decoder_1_out_0), .out_1(decoder_1_out_1), .out_2(decoder_1_out_2),
    .out_3(decoder_1_out_3), .out_4(decoder_1_out_4), .out_5(decoder_1_out_5), .out_6(decoder_1_out_6),
    .out_7(decoder_1_out_7), .out_8(decoder_1_out_8), .out_9(decoder_1_out_9), .out_10(decoder_1_out_10),
    .out_11(decoder_1_out_11), .out_12(decoder_1_out_12), .out_13(decoder_1_out_13),
    .out_14(decoder_1_out_14), .out_15(decoder_1_out_15));
  and and_1 (EN0, decoder_1_out_0, EN);
  and and_2 (EN1, decoder_1_out_1, EN);
  and and_3 (EN2, decoder_1_out_2, EN);
  and and_4 (EN3, decoder_1_out_3, EN);
  and and_5 (EN4, decoder_1_out_4, EN);
  and and_6 (EN5, decoder_1_out_5, EN);
  and and_7 (EN6, decoder_1_out_6, EN);
  and and_8 (EN7, decoder_1_out_7, EN);
  and and_9 (EN8, decoder_1_out_8, EN);
  and and_10 (EN9, decoder_1_out_9, EN);
  and and_11 (EN10, decoder_1_out_10, EN);
  and and_12 (EN11, decoder_1_out_11, EN);
  and and_13 (EN12, decoder_1_out_12, EN);
  and and_14 (EN13, decoder_1_out_13, EN);
  and and_15 (EN14, decoder_1_out_14, EN);
  and and_16 (EN15, decoder_1_out_15, EN);
endmodule
