// Digital circuit decoder-part2.dig as structural Verilog
module decoder_part2 (
  input  [31:0] IW,
  output RFW,
  output [1:0] EXTop,
  output ALUsrcB,
  output [3:0] ALUop,
  output [1:0] PCsel,
  output [1:0] RR0sel,
  output RR1sel,
  output WRsel,
  output WDsel,
  output RR2sel,
  output SHsel,
  output ldr,
  output str,
  output dp_i,
  output sdt_i,
  output CPSRW,
  output mul_i,
  output \byte 
);

  wire add_i, add_r, and_i, and_r, b, bl, bx, cmp_i, cmp_r, comparator_1_eq, comparator_2_eq,
       comparator_3_eq, CPSRW_t, ldr_i, ldr_r, ldrb_i, ldrb_r, mov_i, mov_r, mul, multiplexer_1_out,
       negation_1_na, rsb_i, rsb_r, shift_i, str_i, str_r, strb_i, strb_r, sub_i, sub_r;
  wire [1:0] rom_1_d;
  wire [4:0] priorityencoder_1_num;

  Comparator #(.Bits(8)) addr_r (.a(IW[27:20]), .b(8'h8), .eq(add_r));  // open: gt, lt
  Comparator #(.Bits(8)) u_sub_r (.a(IW[27:20]), .b(8'h4), .eq(sub_r));  // open: gt, lt
  Comparator #(.Bits(8)) u_rsb_r (.a(IW[27:20]), .b(8'h6), .eq(rsb_r));  // open: gt, lt
  Comparator #(.Bits(8)) u_mov_r (.a(IW[27:20]), .b(8'h1a), .eq(mov_r));  // open: gt, lt
  Comparator #(.Bits(8)) u_cmp_r (.a(IW[27:20]), .b(8'h15), .eq(cmp_r));  // open: gt, lt
  Comparator #(.Bits(8)) u_and_r (.a(IW[27:20]), .b({8{1'b0}}), .eq(and_r));  // open: gt, lt
  Comparator #(.Bits(8)) u_str_r (.a(IW[27:20]), .b(8'h78), .eq(str_r));  // open: gt, lt
  Comparator #(.Bits(8)) u_ldr_r (.a(IW[27:20]), .b(8'h79), .eq(ldr_r));  // open: gt, lt
  Comparator #(.Bits(8)) u_strb_r (.a(IW[27:20]), .b(8'h7c), .eq(strb_r));  // open: gt, lt
  Comparator #(.Bits(8)) u_ldrb_r (.a(IW[27:20]), .b(8'h7d), .eq(ldrb_r));  // open: gt, lt
  PriorityEncoder #(.Selector_Bits(5)) priorityencoder_1 (
    .in0(add_r), .in1(add_i), .in2(sub_r), .in3(sub_i), .in4(rsb_r), .in5(rsb_i), .in6(mov_r), .in7(mov_i),
    .in8(cmp_r), .in9(cmp_i), .in10(and_r), .in11(and_i), .in12(str_r), .in13(str_i), .in14(ldr_r),
    .in15(ldr_i), .in16(strb_r), .in17(strb_i), .in18(ldrb_r), .in19(ldrb_i), .in20(mul), .in21(b),
    .in22(bl), .in23(bx), .in24(1'b0), .in25(1'b0), .in26(1'b0), .in27(1'b0), .in28(1'b0), .in29(1'b0),
    .in30(1'b0), .in31(1'b0), .num(priorityencoder_1_num));  // open: any
  shift_inst shift_inst_1 (.i(priorityencoder_1_num), .shift(shift_i));
  ROM #(.AddrBits(5), .Bits(24)) rom_1 (
    .A(priorityencoder_1_num), .sel(1'b1),
    .D({RFW, EXTop, ALUsrcB, ALUop, PCsel, RR0sel, RR1sel, WRsel, WDsel, CPSRW_t, str, ldr, \byte , sdt_i, dp_i, mul_i, rom_1_d}));
  Comparator #(.Bits(8)) addr_i (.a(IW[27:20]), .b(8'h28), .eq(add_i));  // open: gt, lt
  Comparator #(.Bits(8)) u_sub_i (.a(IW[27:20]), .b(8'h24), .eq(sub_i));  // open: gt, lt
  Comparator #(.Bits(8)) u_rsb_i (.a(IW[27:20]), .b(8'h26), .eq(rsb_i));  // open: gt, lt
  Comparator #(.Bits(8)) u_mov_i (.a(IW[27:20]), .b(8'h3a), .eq(mov_i));  // open: gt, lt
  Comparator #(.Bits(8)) u_cmp_i (.a(IW[27:20]), .b(8'h35), .eq(cmp_i));  // open: gt, lt
  Comparator #(.Bits(8)) u_and_i (.a(IW[27:20]), .b(8'h20), .eq(and_i));  // open: gt, lt
  Comparator #(.Bits(8)) u_str_i (.a(IW[27:20]), .b(8'h58), .eq(str_i));  // open: gt, lt
  Comparator #(.Bits(8)) u_ldr_i (.a(IW[27:20]), .b(8'h59), .eq(ldr_i));  // open: gt, lt
  Comparator #(.Bits(8)) u_strb_i (.a(IW[27:20]), .b(8'h5c), .eq(strb_i));  // open: gt, lt
  Comparator #(.Bits(8)) u_ldrb_i (.a(IW[27:20]), .b(8'h5d), .eq(ldrb_i));  // open: gt, lt
  Comparator #(.Bits(8)) comparator_1 (.a(IW[27:20]), .b({8{1'b0}}), .eq(comparator_1_eq));  // open: gt, lt
  Comparator #(.Bits(4)) comparator_2 (.a(IW[7:4]), .b(4'b1001), .eq(comparator_2_eq));  // open: gt, lt
  Comparator #(.Bits(4)) u_b (.a(IW[27:24]), .b(4'b1010), .eq(b));  // open: gt, lt
  Comparator #(.Bits(24)) u_bx (.a(IW[27:4]), .b(24'h12fff1), .eq(bx));  // open: gt, lt
  and and_1 (mul, comparator_1_eq, comparator_2_eq);
  Comparator #(.Bits(8)) comparator_3 (.a(IW[11:4]), .b({8{1'b0}}), .eq(comparator_3_eq));  // open: gt, lt
  or or_1 (CPSRW, CPSRW_t, b, bl);
  Multiplexer multiplexer_1 (.sel(IW[4]), .in_0(1'b0), .in_1(1'b1), .out(multiplexer_1_out));
  negation negation_1 (.a(comparator_3_eq), .na(negation_1_na));
  negation negation_2 (.a(multiplexer_1_out), .na(RR2sel));
  and and_2 (SHsel, shift_i, negation_1_na);
  // Probe on RFW
  // Probe on EXTop
  // Probe on ALUsrcB
  // Probe on ALUop
  // Probe on PCsel
  // Probe on RR0sel
  // Probe on RR1sel
  // Probe on WRsel
  // Probe on WDsel
  Comparator #(.Bits(4)) u_bl (.a(IW[27:24]), .b(4'b1011), .eq(bl));  // open: gt, lt
  // Probe on RR2sel
  // Probe on SHsel

  // Other names for the same wires on the sheet: bits4_4 = IW[4]; bits7_4[3:0] = IW[7:4]; bits11_4[7:0] = IW[11:4];
  //   bits27_4[23:0] = IW[27:4]; bits27_20[7:0] = IW[27:20]; bits27_24[3:0] = IW[27:24]

  // Notes on the sheet:
  //   contents of rom_1 (hex, n*v repeats v):
  //   800008,900008,810008,910008,820008,920008,840008,940008,10108
  //   ,110108,850008,950008,8000d0,1000d0,800050,900050,8000f0,1000f0
  //   ,800070,900070,830004,505000,d05600,8000
  //   mul
endmodule
