// Digital circuit digital-register-clr.dig as structural Verilog
module digital_register_clr (
  input  [31:0] D,
  input  CLK,
  input  EN,
  input  CLR,
  output [31:0] Q
);

  wire or_1_out;
  wire [31:0] multiplexer_1_out;

  Multiplexer #(.Bits(32)) multiplexer_1 (.sel(CLR), .in_0(D), .in_1({32{1'b0}}), .out(multiplexer_1_out));
  or or_1 (or_1_out, EN, CLR);
  Register #(.Bits(32)) register_1 (.D(multiplexer_1_out), .C(CLK), .en(or_1_out), .Q(Q));
endmodule
