// Digital circuit extension-unit.dig as structural Verilog
module extension_unit (
  input  [31:0] IW,
  input  [1:0] EXTop,
  output [31:0] extimm
);

  wire [31:0] b_1_d, dp_1_d, sdt_1_d;
  wire [63:0] mul_1_mul;

  DP dp_1 (.IW(IW), .D(dp_1_d));
  SDT sdt_1 (.IW(IW), .D(sdt_1_d));
  B b_1 (.IW(IW), .D(b_1_d));  // open: D_1
  Mul #(.Bits(32)) mul_1 (.a(b_1_d), .b(32'h4), .mul(mul_1_mul));
  Multiplexer #(.Selector_Bits(2), .Bits(32)) multiplexer_1 (
    .sel(EXTop), .in_0(dp_1_d), .in_1(sdt_1_d), .in_2(mul_1_mul[31:0]), .in_3({32{1'b0}}), .out(extimm));
endmodule
