// Digital circuit inst-type.dig as structural Verilog
module inst_type (
  input  dp,
  input  sdt,
  input  mul,
  output [1:0] itype
);

  wire [1:0] and_1_out, and_2_out;
  wire [3:0] mul_1_mul;

  assign and_1_out = ~{1'b0, dp} & ~{1'b0, mul} & {1'b0, sdt};  // And and_1, 2 bits wide
  assign and_2_out = ~{1'b0, dp} & {1'b0, mul} & ~{1'b0, sdt};  // And and_2, 2 bits wide
  Mul #(.Bits(2)) mul_1 (.a(and_1_out), .b(2'b10), .mul(mul_1_mul));
  Add #(.Bits(2)) add_1 (.a(mul_1_mul[1:0]), .b(and_2_out), .c_i(1'b0), .s(itype));  // open: c_o
endmodule
