// Digital circuit project06.dig as structural Verilog
module project06 (
  input  CLR,
  input  CLK,
  input  [4:0] PROG,
  output DONE,
  output [31:0] R0,
  output [31:0] R2
);

  wire a_mul, ALUsrcB, \byte , C, CLK_t, dp_i, i_dp, ldr, mul_i, N, RFW, RR1sel, RR2sel, sdt_i, SHsel, str,
       V, WDsel, WRsel, Z;
  wire [1:0] EXTop, itype, PCsel, RR0sel;
  wire [3:0] _3_0, _11_8, _15_12, _19_16, ALUop, cond, des, multiplexer_5_out, multiplexer_6_out,
       multiplexer_7_out, multiplexer_8_out, NZCV, rr0, rr1;
  wire [23:4] b_offset;
  wire [27:24] iw;
  wire [31:0] add_1_s, add_2_s, alu_1_r, DD, extension_unit_1_extimm, multiplexer_1_out, multiplexer_9_out,
       multiplexer_10_out, multiplexer_11_out, multiplexer_12_out, pc_1_q, r1, r3, r4, r5, r6, r7, r8, r9,
       r10, r11, r12, r13, r14, r15, ramdualport_1_d, RD2, register_file_1_rd0, register_file_1_rd1,
       shifter_1_r;
  wire [63:0] mul_1_mul;

  and and_1 (CLK_t, CLK, ~DONE);  // And
  PC pc_1 (.D(multiplexer_1_out), .CLK(CLK_t), .EN(1'b1), .CLR(CLR), .Q(pc_1_q));
  Multiplexer #(.Selector_Bits(2), .Bits(32)) multiplexer_1 (
    .sel(PCsel), .in_0(add_1_s), .in_1(multiplexer_11_out), .in_2(register_file_1_rd1), .in_3({32{1'b0}}),
    .out(multiplexer_1_out));
  // Probe on {cond, iw[27:26], i_dp, iw[24], b_offset[23:22], a_mul, b_offset[20], _19_16, _15_12, _11_8, b_offset[7:4], _3_0}
  control_unit control_unit_1 (
    .IW({cond, iw[27:26], i_dp, iw[24], b_offset[23:22], a_mul, b_offset[20], _19_16, _15_12, _11_8, b_offset[7:4], _3_0}),
    .NZCV(NZCV), .CLK(CLK_t), .RFW(RFW), .EXTop(EXTop), .ALUsrcB(ALUsrcB), .ALUop(ALUop), .PCsel(PCsel),
    .RR0sel(RR0sel), .RR1sel(RR1sel), .RR2sel(RR2sel), .WRsel(WRsel), .WDsel(WDsel), .SHsel(SHsel),
    .str(str), .ldr(ldr), .\byte (\byte ), .sdt_i(sdt_i), .dp_i(dp_i), .mul_i(mul_i));
  instruction_memory instruction_memory_1 (
    .A(pc_1_q[8:2]), .PN(PROG),
    .D({cond, iw[27:26], i_dp, iw[24], b_offset[23:22], a_mul, b_offset[20], _19_16, _15_12, _11_8, b_offset[7:4], _3_0}));
  Add #(.Bits(32)) add_1 (.a(pc_1_q), .b(32'h4), .c_i(1'b0), .s(add_1_s));  // open: c_o
  Add #(.Bits(32)) add_2 (.a(add_1_s), .b(32'h4), .c_i(1'b0), .s(add_2_s));  // open: c_o
  // Probe on R0
  // Probe on r1
  // Probe on R2
  // Probe on r3
  inst_type inst_type_1 (.dp(dp_i), .mul(mul_i), .sdt(sdt_i), .itype(itype));
  Multiplexer #(.Selector_Bits(2), .Bits(4)) multiplexer_2 (
    .sel(itype), .in_0(_15_12), .in_1(_19_16), .in_2(_15_12), .in_3(4'b0000), .out(des));
  Multiplexer #(.Selector_Bits(2), .Bits(4)) multiplexer_3 (
    .sel(itype), .in_0(_19_16), .in_1(_3_0), .in_2(_19_16), .in_3(4'b0000), .out(rr0));
  Multiplexer #(.Selector_Bits(2), .Bits(4)) multiplexer_4 (
    .sel(itype), .in_0(_3_0), .in_1(_11_8), .in_2(_3_0), .in_3(4'b0000), .out(rr1));
  // Probe on cond
  // Probe on cond
  // Probe on cond
  // Probe on cond
  // Probe on iw[27:26]
  // Probe on {iw[27:26], i_dp, iw[24], b_offset[23]}
  // Probe on iw[27:26]
  // Probe on {iw[27:26], i_dp}
  // Probe on r4
  // Probe on r5
  // Probe on r6
  // Probe on r7
  // Probe on i_dp
  // Probe on i_dp
  // Probe on iw[24]
  // Probe on a_mul
  Multiplexer #(.Selector_Bits(2), .Bits(4)) multiplexer_5 (
    .sel(RR0sel), .in_0(rr0), .in_1(4'b1111), .in_2(4'b0000), .in_3(4'b0000), .out(multiplexer_5_out));
  Multiplexer #(.Bits(4)) multiplexer_6 (.sel(RR1sel), .in_0(rr1), .in_1(4'b0000), .out(multiplexer_6_out));
  Multiplexer #(.Bits(4)) multiplexer_7 (.sel(RR2sel), .in_0(_11_8), .in_1(4'b0000), .out(multiplexer_7_out));
  Multiplexer #(.Bits(4)) multiplexer_8 (.sel(WRsel), .in_0(des), .in_1(4'b1110), .out(multiplexer_8_out));
  Multiplexer #(.Bits(32)) multiplexer_9 (
    .sel(WDsel), .in_0(multiplexer_11_out), .in_1(add_1_s), .out(multiplexer_9_out));
  // Probe on r8
  // Probe on r9
  // Probe on r10
  // Probe on r11
  // Probe on {iw[24], b_offset[23:22], a_mul}
  // Probe on b_offset[20]
  // Probe on iw[24]
  // Probe on {b_offset[23:22], a_mul, b_offset[20], _19_16, _15_12, _11_8, b_offset[7:4], _3_0}
  register_file register_file_1 (
    .ReadReg0(multiplexer_5_out), .ReadReg1(multiplexer_6_out), .ReadReg2(multiplexer_7_out),
    .WriteReg(multiplexer_8_out), .WriteData(multiplexer_9_out), .WriteEn(RFW), .PC(add_2_s), .CLK(CLK_t),
    .CLR(CLR), .RD0(register_file_1_rd0), .RD1(register_file_1_rd1), .RD2(RD2), .DD(DD), .r0(R0), .r1(r1),
    .r2(R2), .r3(r3), .r4(r4), .r5(r5), .r6(r6), .r7(r7), .r8(r8), .r9(r9), .r10(r10), .r11(r11), .r12(r12),
    .r13(r13), .r14(r14), .r15(r15));
  // Probe on b_offset[20]
  // Probe on _19_16
  // Probe on b_offset[23]
  // Probe on _19_16
  // Probe on _15_12
  // Probe on b_offset[22]
  // Probe on _15_12
  // Probe on a_mul
  // Probe on r12
  // Probe on r13
  // Probe on r14
  // Probe on r15
  // Probe on _3_0
  // Probe on _11_8
  // Probe on b_offset[7:4]
  // Probe on b_offset[20]
  shifter shifter_1 (
    .SHsel(SHsel), .RR2sel(RR2sel),
    .iw({cond, iw[27:26], i_dp, iw[24], b_offset[23:22], a_mul, b_offset[20], _19_16, _15_12, _11_8, b_offset[7:4], _3_0}),
    .RS(RD2), .D(register_file_1_rd1), .R(shifter_1_r));
  extension_unit extension_unit_1 (
    .EXTop(EXTop),
    .IW({cond, iw[27:26], i_dp, iw[24], b_offset[23:22], a_mul, b_offset[20], _19_16, _15_12, _11_8, b_offset[7:4], _3_0}),
    .extimm(extension_unit_1_extimm));
  // Probe on N
  // Probe on Z
  // Probe on C
  // Probe on V
  // Probe on _3_0
  // Probe on _19_16
  // Probe on _15_12
  Multiplexer #(.Bits(32)) multiplexer_10 (
    .sel(ALUsrcB), .in_0(shifter_1_r), .in_1(extension_unit_1_extimm), .out(multiplexer_10_out));
  // Probe on _3_0
  Mul #(.Bits(32)) mul_1 (.a(multiplexer_10_out), .b(32'h4), .mul(mul_1_mul));
  Multiplexer #(.Bits(32)) multiplexer_11 (
    .sel(sdt_i), .in_0(alu_1_r), .in_1(ramdualport_1_d), .out(multiplexer_11_out));
  // Probe on {_11_8, b_offset[7:4], _3_0}
  Comparator #(.Bits(32)) comparator_1 (
    .a({cond, iw[27:26], i_dp, iw[24], b_offset[23:22], a_mul, b_offset[20], _19_16, _15_12, _11_8, b_offset[7:4], _3_0}),
    .b(32'he2800000), .eq(DONE));  // open: gt, lt
  Multiplexer #(.Bits(32)) multiplexer_12 (
    .sel(\byte ), .in_0(multiplexer_10_out), .in_1(mul_1_mul[31:0]), .out(multiplexer_12_out));
  ALU alu_1 (
    .A(register_file_1_rd0), .B(multiplexer_12_out), .ALUOp(ALUop), .R(alu_1_r), .N(N), .Z(Z), .C(C), .V(V),
    .NZCV(NZCV));
  // Probe on ALUop
  // Probe on alu_1_r
  RAMDualPort #(.AddrBits(8), .Bits(32)) ramdualport_1 (
    .A(alu_1_r[9:2]), .Din(DD), .str(str), .C(CLK_t), .ld(ldr), .D(ramdualport_1_d));

  // Other names for the same wires on the sheet: b_offset (some bits) = {a_mul, _19_16, _15_12, _11_8, _3_0};
  //   imm[7:0] = {b_offset[7:4], _3_0}; immoff[11:0] = {_11_8, b_offset[7:4], _3_0};
  //   iw (some bits) = {cond, i_dp, b_offset[23:22], a_mul, b_offset[20], _19_16, _15_12, _11_8, b_offset[7:4], _3_0};
  //   rm[3:0] = _3_0; rm_mul[3:0] = _3_0; opmul4[3:0] = b_offset[7:4]; rs_mul[3:0] = _11_8; rd[3:0] = _15_12;
  //   rn_mul[3:0] = _15_12; rd_mul[3:0] = _19_16; rn[3:0] = _19_16; l_sdt = b_offset[20]; s_dp = b_offset[20];
  //   s_mul = b_offset[20]; opc[3:0] = {iw[24], b_offset[23:22], a_mul}; w_sdt = a_mul; b_sdt = b_offset[22];
  //   opmul_6[4:0] = {iw[27:26], i_dp, iw[24], b_offset[23]}; u_sdt = b_offset[23]; l_b = iw[24]; p_sdt = iw[24];
  //   i_sdt = i_dp; opb3[2:0] = {iw[27:26], i_dp}; op2[1:0] = iw[27:26]; opmul2[1:0] = iw[27:26]

  // Notes on the sheet:
  //   CLK: Hz: 200
  //   PROG: default 18
  //   DP
  //   MUL
  //   SDT
  //   B
  //   IP
  //   SP
  //   LR
  //   PC
endmodule
