// Digital circuit register-file.dig as structural Verilog
module register_file (
  input  [3:0] ReadReg0,
  input  [3:0] ReadReg1,
  input  [3:0] WriteReg,
  input  [31:0] WriteData,
  input  WriteEn,
  input  [31:0] PC,
  input  CLK,
  input  CLR,
  input  [3:0] ReadReg2,
  output [31:0] RD0,
  output [31:0] RD1,
  output [31:0] r0,
  output [31:0] r1,
  output [31:0] r2,
  output [31:0] r3,
  output [31:0] r4,
  output [31:0] r5,
  output [31:0] r6,
  output [31:0] r7,
  output [31:0] r8,
  output [31:0] r9,
  output [31:0] r10,
  output [31:0] r11,
  output [31:0] r12,
  output [31:0] r13,
  output [31:0] r14,
  output [31:0] r15,
  output [31:0] RD2,
  output [31:0] DD
);

  wire EN0, EN1, EN2, EN3, EN4, EN5, EN6, EN7, EN8, EN9, EN10, EN11, EN12, EN13, EN14;

  decoder_en decoder_en_1 (
    .SEL(WriteReg), .EN(WriteEn), .EN0(EN0), .EN1(EN1), .EN2(EN2), .EN3(EN3), .EN4(EN4), .EN5(EN5),
    .EN6(EN6), .EN7(EN7), .EN8(EN8), .EN9(EN9), .EN10(EN10), .EN11(EN11), .EN12(EN12), .EN13(EN13),
    .EN14(EN14));  // open: EN15
  digital_register_clr digital_register_clr_1 (.D(WriteData), .CLK(CLK), .EN(EN0), .CLR(CLR), .Q(r0));
  digital_register_clr digital_register_clr_2 (.D(WriteData), .CLK(CLK), .EN(EN1), .CLR(CLR), .Q(r1));
  digital_register_clr digital_register_clr_3 (.D(WriteData), .CLK(CLK), .EN(EN2), .CLR(CLR), .Q(r2));
  digital_register_clr digital_register_clr_4 (.D(WriteData), .CLK(CLK), .EN(EN3), .CLR(CLR), .Q(r3));
  digital_register_clr digital_register_clr_5 (.D(WriteData), .CLK(CLK), .EN(EN4), .CLR(CLR), .Q(r4));
  digital_register_clr digital_register_clr_6 (.D(WriteData), .CLK(CLK), .EN(EN5), .CLR(CLR), .Q(r5));
  digital_register_clr digital_register_clr_7 (.D(WriteData), .CLK(CLK), .EN(EN6), .CLR(CLR), .Q(r6));
  digital_register_clr digital_register_clr_8 (.D(WriteData), .CLK(CLK), .EN(EN7), .CLR(CLR), .Q(r7));
  digital_register_clr digital_register_clr_9 (.D(WriteData), .CLK(CLK), .EN(EN8), .CLR(CLR), .Q(r8));
  digital_register_clr digital_register_clr_10 (.D(WriteData), .CLK(CLK), .EN(EN9), .CLR(CLR), .Q(r9));
  digital_register_clr digital_register_clr_11 (.D(WriteData), .CLK(CLK), .EN(EN10), .CLR(CLR), .Q(r10));
  digital_register_clr digital_register_clr_12 (.D(WriteData), .CLK(CLK), .EN(EN11), .CLR(CLR), .Q(r11));
  digital_register_clr digital_register_clr_13 (.D(WriteData), .CLK(CLK), .EN(EN12), .CLR(CLR), .Q(r12));
  digital_register_clr digital_register_clr_14 (.D(WriteData), .CLK(CLK), .EN(EN13), .CLR(CLR), .Q(r13));
  digital_register_clr digital_register_clr_15 (.D(WriteData), .CLK(CLK), .EN(EN14), .CLR(CLR), .Q(r14));
  Multiplexer #(.Selector_Bits(4), .Bits(32)) multiplexer_1 (
    .sel(ReadReg0), .in_0(r0), .in_1(r1), .in_2(r2), .in_3(r3), .in_4(r4), .in_5(r5), .in_6(r6), .in_7(r7),
    .in_8(r8), .in_9(r9), .in_10(r10), .in_11(r11), .in_12(r12), .in_13(r13), .in_14(r14), .in_15(PC),
    .out(RD0));
  Multiplexer #(.Selector_Bits(4), .Bits(32)) multiplexer_2 (
    .sel(ReadReg1), .in_0(r0), .in_1(r1), .in_2(r2), .in_3(r3), .in_4(r4), .in_5(r5), .in_6(r6), .in_7(r7),
    .in_8(r8), .in_9(r9), .in_10(r10), .in_11(r11), .in_12(r12), .in_13(r13), .in_14(r14), .in_15(PC),
    .out(RD1));
  Multiplexer #(.Selector_Bits(4), .Bits(32)) multiplexer_3 (
    .sel(ReadReg2), .in_0(r0), .in_1(r1), .in_2(r2), .in_3(r3), .in_4(r4), .in_5(r5), .in_6(r6), .in_7(r7),
    .in_8(r8), .in_9(r9), .in_10(r10), .in_11(r11), .in_12(r12), .in_13(r13), .in_14(r14), .in_15(PC),
    .out(RD2));
  Multiplexer #(.Selector_Bits(4), .Bits(32)) multiplexer_4 (
    .sel(WriteReg), .in_0(r0), .in_1(r1), .in_2(r2), .in_3(r3), .in_4(r4), .in_5(r5), .in_6(r6), .in_7(r7),
    .in_8(r8), .in_9(r9), .in_10(r10), .in_11(r11), .in_12(r12), .in_13(r13), .in_14(r14), .in_15(PC),
    .out(DD));

  assign r15 = PC;

  // Other names for the same wires on the sheet: WE = WriteEn; WR[3:0] = WriteReg

  // Notes on the sheet:
  //   WD: contains the value we will
  //   write to WriteReg if WriteEn is high
  //   WE: determines whether we will
  //   update a register in this clock cycle
  //   RR1: selects the register
  //   value to output on RD1
  //   RR0: selects the register value to output on RD0
  //   WR: selects the destination 
  //   register to update
endmodule
