// Digital circuit shift-inst.dig as structural Verilog
module shift_inst (
  input  [4:0] i,
  output shift
);

  wire comparator_1_eq, comparator_2_gt, comparator_3_lt, or_1_out;

  Comparator #(.Bits(5)) comparator_1 (.a(i), .b({5{1'b0}}), .eq(comparator_1_eq));  // open: gt, lt
  Comparator #(.Bits(5)) comparator_2 (.a(i), .b({5{1'b0}}), .gt(comparator_2_gt));  // open: eq, lt
  Comparator #(.Bits(5)) comparator_3 (.a(i), .b(5'b10100), .lt(comparator_3_lt));  // open: gt, eq
  or or_1 (or_1_out, comparator_1_eq, comparator_2_gt);
  and and_1 (shift, or_1_out, comparator_3_lt);
endmodule
