// Digital circuit shifter.dig as structural Verilog
module shifter (
  input  SHsel,
  input  [31:0] iw,
  input  [31:0] RS,
  input  [31:0] D,
  input  RR2sel,
  output [31:0] R
);

  wire [5:0] amount;
  wire [31:0] asr_out, lsl_out, lsr_out, multiplexer_2_out;
  wire [31:6] multiplexer_1_out;

  BarrelShifter #(.Bits(32)) lsl (.in(D), .shift(amount), .out(lsl_out));
  BarrelShifter #(.Bits(32), .direction("right")) lsr (.in(D), .shift(amount), .out(lsr_out));
  BarrelShifter #(.Bits(32), .barrelShifterMode("arithmetic"), .direction("right")) asr (
    .in(D), .shift(amount), .out(asr_out));
  Multiplexer #(.Bits(32)) multiplexer_1 (
    .sel(RR2sel), .in_0(RS), .in_1({{27{1'b0}}, iw[11:7]}), .out({multiplexer_1_out, amount}));
  Multiplexer #(.Selector_Bits(2), .Bits(32)) multiplexer_2 (
    .sel(iw[6:5]), .in_0(lsl_out), .in_1(lsr_out), .in_2(asr_out), .in_3({32{1'b0}}), .out(multiplexer_2_out));
  Multiplexer #(.Bits(32)) multiplexer_3 (.sel(SHsel), .in_0(D), .in_1(multiplexer_2_out), .out(R));

  // Notes on the sheet:
  //   0: no shift
  //   1: apply shift
  //   0: rs
  //   1: imm
  //   The value to shift (rm)
endmodule
